# Fritzing sketch circle (saved by Fritzing 0.9.3b)

parts:
  Orange_Pi_One1 = Orange Pi One [part_number=OPI-ONE]
  元件1 = BME280
  CAMERA1 = TTL Serial JPEG Camera  # not connected

nets:
  N1: Orange_Pi_One1.PA12, 元件1.SDA
  N2: Orange_Pi_One1.PA11, 元件1.SCL
  GND: Orange_Pi_One1.GND, 元件1.GND
  5V: Orange_Pi_One1.5V, 元件1.VIN

custom parts:
  Orange Pi One: It’s an open-source single-board computer. It can run Android 4.4, Ubuntu, Debian, Rasberry Pi Image, as well as the banana pi Image. It uses the AllWinner H3 SoC, and has 512MB DDR3 SDRAM
  TTL Serial JPEG Camera: TTL Serial JPEG Camera with NTSC Out
